# Fritzing sketch arduino_client (saved by Fritzing 0.9.2b)
breadboards: 1
perfboards: 1

parts:
  Part1 = Arduino Uno (Rev3)  # not connected
  Part2 = Arduino Ethernet Shield (Rev3)
  LCD1 = LCD screen  # not connected
  LED1 = LED - 5mm [color="Red (633nm)" package="5 mm [THT]"]
  KEYPAD1 = Membrane Matrix Keypad  # not connected

nets:
  N1: Part2.PWM_D9, LED1.anode
  N2: Part2.GND, LED1.cathode

custom parts:
  Membrane Matrix Keypad: Membrane Matrix 3x4 Keypad
